# Fritzing sketch sketch2 (saved by Fritzing 0.9.3b)
breadboards: 2

parts:
  OLED_I2C1 = OLED 128x64 I2C Monochrome Display
  OLED_I2C2 = OLED 128x64 I2C Monochrome Display
  Part1 = u-blox NEO-6M GPS Breakout
  S1 = Pushbutton [package="[THT]"]
  R1 = Resistor [tolerance=±5% resistance=150 package=THT]
  R2 = Resistor [tolerance=±5% resistance=100 package=THT]
  R3 = Resistor [tolerance=±5% resistance=15 package=THT]
  LED1 = LED - 5mm [color="Yellow (592nm)" package="5 mm [THT]"]
  LED2 = LED - 5mm [color="Red (633nm)" package="5 mm [THT]"]
  LED3 = LED - 5mm [color="Green (560nm)" package="5 mm [THT]"]
  ZS-042_RTC1 = ZS-042 RTC Module
  Amica_NodeMCU_DevKit_1_1 = Amica NodeMCU DevKit 1.0
  HLK-PM2 = HLK-PM01
  U1 = Mini-360 DC-DC Buck converter [package=THT]
  C1 = Ceramic Capacitor [capacitance=100nF package="100 mil [THT, multilayer]"]
  S2 = Toggle Switch [package=THT]
  R4 = Resistor [tolerance=±5% resistance=1k package=THT]
  R5 = Resistor [tolerance=±5% resistance=1k package=THT]

nets:
  N1: OLED_I2C1.SDA, OLED_I2C2.SDA, ZS-042_RTC1.SDA, Amica_NodeMCU_DevKit_1_1.pin_13
  N2: OLED_I2C1.SCK, OLED_I2C2.SCK, ZS-042_RTC1.SCL, Amica_NodeMCU_DevKit_1_1.pin_14
  VDD: OLED_I2C1.VDD, OLED_I2C2.VDD, Part1.VCC, ZS-042_RTC1.VCC, U1.OUT+, C1.0, S2.L2, R4.Pin_0
  GND: OLED_I2C1.GND, OLED_I2C2.GND, Part1.GND, S1.Pin_1, S1.Pin_2, LED1.cathode, LED2.cathode, LED3.cathode, ZS-042_RTC1.GND, Amica_NodeMCU_DevKit_1_1.pin2, Amica_NodeMCU_DevKit_1_1.pin_9, Amica_NodeMCU_DevKit_1_1.pin_25, Amica_NodeMCU_DevKit_1_1.pin_29, HLK-PM2.-Vo, U1.IN-, U1.OUT-, C1.1, R5.Pin_1
  N3: Part1.TXD, Amica_NodeMCU_DevKit_1_1.pin6
  N4: Part1.RXD, Amica_NodeMCU_DevKit_1_1.pin5
  N5: Part1.PPS, Amica_NodeMCU_DevKit_1_1.pin7
  N6: S1.Pin_3, S1.Pin_4, Amica_NodeMCU_DevKit_1_1.pin_11
  N7: R1.Pin_0, LED2.anode
  N8: R1.Pin_1, Amica_NodeMCU_DevKit_1_1.pin_19
  N9: R2.Pin_0, LED3.anode
  N10: R2.Pin_1, Amica_NodeMCU_DevKit_1_1.pin_12
  N11: R3.Pin_0, LED1.anode
  N12: R3.Pin_1, Amica_NodeMCU_DevKit_1_1.pin8
  N13: Amica_NodeMCU_DevKit_1_1.pin1, Amica_NodeMCU_DevKit_1_1.pin_10, Amica_NodeMCU_DevKit_1_1.pin_26
  N14: Amica_NodeMCU_DevKit_1_1.pin_16, S2.COM
  N15: Amica_NodeMCU_DevKit_1_1.pin_30, HLK-PM2.+Vo, U1.IN+
  N16: S2.L1, R4.Pin_1, R5.Pin_0

notes:
  GROUND

custom parts:
  Amica NodeMCU DevKit 1.0: Amica NodeMCU DEVKIT 1.0 Development Kit based on ESP8266 ESP-12E, integating GPIO, PWM, IIC, 1-Wire and ADC all in one board.
  Mini-360 DC-DC Buck converter: Mini-360 DC-DC Buck converter. Tiny buck step down voltage converter, input voltage 4.75 to 23V output 1 to 17V adjustable. Available from ebay and the like.
